# Fritzing sketch Sketch_BluetoothHC05_Fritzing (saved by Fritzing 0.9.4)
breadboards: 1

parts:
  Componente1 = Bluetooth HC-05 Macho
  Componente2 = Arduino Uno (Rev3) - ICSP

nets:
  N1: Componente1.TXD, Componente2.D0/RX
  N2: Componente1.RXD, Componente2.D1/TX
  VCC: Componente1.VCC, Componente2.5V
  GND: Componente1.GND, Componente2.GND
